# Fritzing sketch Smart_Dam_circuito_draft (saved by Fritzing 0.9.3b)
breadboards: 1

parts:
  Adafruit_HUZZAH_ESP8266_Breakout1 = Adafruit HUZZAH ESP8266 Breakout [part_number=2471]
  Componente1 = Bluetooth HC-05 Macho
  J1 = Basic Servo
  LED1 = smd LED [color="Green (570nm)" package="0603 [SMD]"]
  LED2 = smd LED [color="Green (570nm)" package="0603 [SMD]"]
  hc-sr1 = hc-sr04
  Componente2 = Arduino Uno (Rev3)

nets:
  GND: Adafruit_HUZZAH_ESP8266_Breakout1.GND, LED2.cathode, hc-sr1.GND
  N1: Adafruit_HUZZAH_ESP8266_Breakout1.#16, LED2.anode
  N2: Adafruit_HUZZAH_ESP8266_Breakout1.#4, hc-sr1.Echo
  N3: Adafruit_HUZZAH_ESP8266_Breakout1.#2, hc-sr1.Trig
  N4: Componente1.TXD, Componente2.D3_PWM
  N5: Componente1.RXD, Componente2.D2
  VCC: Componente1.VCC, J1.vcc, hc-sr1.VCC, Componente2.5V
  GND_2: Componente1.GND, J1.gnd, Componente2.GND
  N6: J1.pulse, Componente2.D9_PWM
  N7: LED1.anode, Componente2.D10_PWM/SS
